// Logisim project chapter1.circ as structural Verilog
module Not (
  input  in,
  output out
);

  nand nand_1 (out, in, in);
endmodule

module And (
  input  a,
  input  b,
  output out
);

  wire nand_1_out;

  nand nand_1 (nand_1_out, a, b);
  not not_1 (out, nand_1_out);

  // Notes on the sheet:
  //   nandAB
endmodule

module Or (
  input  a,
  input  b,
  output out
);

  wire not_1_out, not_2_out;

  not not_1 (not_1_out, a);
  not not_2 (not_2_out, b);
  nand nand_1 (out, not_1_out, not_2_out);

  // Notes on the sheet:
  //   notA
  //   notB
endmodule

module Xor (
  input  a,
  input  b,
  output out
);

  wire nand_1_out, or_1_out;

  nand nand_1 (nand_1_out, a, b);
  or or_1 (or_1_out, a, b);
  and and_1 (out, nand_1_out, or_1_out);

  // Notes on the sheet:
  //   nandAB
  //   orAB
endmodule

module Mux (
  input  a,
  input  b,
  input  sel,
  output out
);

  wire and_1_out, and_2_out, not_1_out, or_1_out;

  not not_1 (not_1_out, sel);
  and and_1 (and_1_out, a, not_1_out);
  and and_2 (and_2_out, b, sel);
  or or_1 (or_1_out, and_1_out, and_2_out);

  // Notes on the sheet:
  //   notSel
  //   muxA
  //   muxB
endmodule

module DMux (
  input  in,
  input  sel,
  output a,
  output b
);

  wire not_1_out;

  not not_1 (not_1_out, sel);
  and and_1 (a, not_1_out, in);
  and and_2 (b, in, sel);

  // Notes on the sheet:
  //   notSel
endmodule

module Not16 (
  input  [15:0] in,
  output [15:0] out
);

  assign out = ~in;  // NOT_Gate not_1, 16 bits wide
endmodule

module And16 (
  input  [15:0] a,
  input  [15:0] b,
  output [15:0] out
);

  assign out = a & b;  // AND_Gate and_1, 16 bits wide
endmodule

module Or16 (
  input  [15:0] a,
  input  [15:0] b,
  output [15:0] out
);

  assign out = a | b;  // OR_Gate or_1, 16 bits wide
endmodule

module Mux16 (
  input  [15:0] a,
  input  [15:0] b,
  input  sel,
  output [15:0] out
);

  Multiplexer #(.width(16), .enable("false")) multiplexer_1 (.in0(a), .in1(b), .out(out), .sel(sel));
endmodule

module Or8Way (
  input  [7:0] in,
  input  out
);

  wire or_1_out, or_2_out, or_3_out, or_4_out, or_5_out, or_6_out;

  or or_1 (or_1_out, in[0], in[1]);
  or or_2 (or_2_out, in[2], in[3]);
  or or_3 (or_3_out, in[4], in[5]);
  or or_4 (or_4_out, in[6], in[7]);
  or or_5 (or_5_out, or_1_out, or_2_out);
  or or_6 (or_6_out, or_3_out, or_4_out);
  or or_7 (out, or_5_out, or_6_out);

  // Notes on the sheet:
  //   out01
  //   out23
  //   out45
  //   out67
  //   out03
  //   out47
endmodule

module Mux4Way16 (
  input  [15:0] a,
  input  [15:0] b,
  input  [15:0] c,
  input  [15:0] d,
  input  [1:0] sel,
  output [15:0] a_2
);

  wire [15:0] multiplexer_1_out, multiplexer_2_out;

  Multiplexer #(.width(16), .enable("false")) multiplexer_1 (.in0(a), .in1(b), .out(multiplexer_1_out), .sel(sel[0]));
  Multiplexer #(.width(16), .enable("false")) multiplexer_2 (.in0(c), .in1(d), .out(multiplexer_2_out), .sel(sel[0]));
  Multiplexer #(.width(16), .enable("false")) multiplexer_3 (
    .in0(multiplexer_1_out), .in1(multiplexer_2_out), .out(a_2), .sel(sel[1]));

  // Notes on the sheet:
  //   muxAB
  //   muxCD
endmodule

module Mux8Way16 (
  input  [15:0] a,
  input  [15:0] b,
  input  [15:0] c,
  input  [15:0] d,
  input  [15:0] d_2,
  input  [15:0] e,
  input  [15:0] f,
  input  [15:0] g,
  input  [2:0] sel,
  output [15:0] a_2
);

  wire [15:0] multiplexer_1_out, multiplexer_2_out;

  Multiplexer #(.select(2), .width(16), .enable("false")) multiplexer_1 (
    .in0(a), .in1(b), .in2(c), .in3(d), .out(multiplexer_1_out), .sel(sel[2:1]));
  Multiplexer #(.select(2), .width(16), .enable("false")) multiplexer_2 (
    .in0(d_2), .in1(e), .in2(f), .in3(g), .out(multiplexer_2_out), .sel(sel[2:1]));
  Multiplexer #(.width(16), .enable("false")) multiplexer_3 (
    .in0(multiplexer_1_out), .in1(multiplexer_2_out), .out(a_2), .sel(sel[0]));

  // Notes on the sheet:
  //   MuxAD
  //   MuxDG
endmodule

module DMux4Way (
  input  in,
  input  [1:0] in_2,
  output a,
  output b,
  output c,
  output d
);

  wire demultiplexer_1_out0, demultiplexer_1_out1;

  Demultiplexer #(.enable("false")) demultiplexer_1 (
    .out0(demultiplexer_1_out0), .out1(demultiplexer_1_out1), .in(in), .sel(in_2[1]));
  Demultiplexer #(.enable("false")) demultiplexer_2 (.out0(a), .out1(b), .in(demultiplexer_1_out0), .sel(in_2[0]));
  Demultiplexer #(.enable("false")) demultiplexer_3 (.out0(c), .out1(d), .in(demultiplexer_1_out1), .sel(in_2[0]));

  // Notes on the sheet:
  //   dmuxab
  //   dmuxcd
endmodule

module DMux8Way (
  input  in,
  input  [2:0] in_2,
  output a,
  output b,
  output c,
  output d,
  output e,
  output f,
  output g,
  output g_2
);

  wire demultiplexer_1_out0, demultiplexer_1_out1;

  Demultiplexer #(.enable("false")) demultiplexer_1 (
    .out0(demultiplexer_1_out0), .out1(demultiplexer_1_out1), .in(in), .sel(in_2[2]));
  Demultiplexer #(.select(2), .enable("false")) demultiplexer_2 (
    .out0(a), .out1(b), .out2(c), .out3(d), .in(demultiplexer_1_out0), .sel(in_2[1:0]));
  Demultiplexer #(.select(2), .enable("false")) demultiplexer_3 (
    .out0(e), .out1(f), .out2(g), .out3(g_2), .in(demultiplexer_1_out1), .sel(in_2[1:0]));

  // Notes on the sheet:
  //   dmuxab
  //   dmuxeg
endmodule
