// Logisim project chapter2.circ as structural Verilog
module HalfAdder (
  input  a,
  input  b,
  output sum,
  output carry
);

  xor xor_1 (sum, b, a);
  and and_1 (carry, b, a);
endmodule

module FullAdder (
  input  c,
  input  b,
  input  a,
  output sum,
  output carry
);

  wire halfadder_1_carry, halfadder_1_sum, not_1_out, or_1_out, xor_1_out;

  HalfAdder halfadder_1 (.a(b), .b(c), .sum(halfadder_1_sum), .carry(halfadder_1_carry));
  xor xor_1 (xor_1_out, b, c);
  or or_1 (or_1_out, c, b);
  not not_1 (not_1_out, xor_1_out);
  Multiplexer #(.enable("false")) multiplexer_1 (.in0(halfadder_1_sum), .in1(not_1_out), .out(sum), .sel(a));
  Multiplexer #(.enable("false")) multiplexer_2 (.in0(halfadder_1_carry), .in1(or_1_out), .out(carry), .sel(a));

  // Notes on the sheet:
  //   xorBC
  //   sumBC
  //   carryBC
  //   orBC
  //   notxorbc
endmodule

module Add16 (
  input  [15:0] a,
  input  [15:0] b,
  output [15:0] out
);

  wire fulladder_1_carry, fulladder_2_carry, fulladder_3_carry, fulladder_4_carry, fulladder_5_carry,
       fulladder_6_carry, fulladder_7_carry, fulladder_8_carry, fulladder_9_carry, fulladder_10_carry,
       fulladder_11_carry, fulladder_12_carry, fulladder_13_carry, fulladder_14_carry, halfadder_1_carry;

  HalfAdder halfadder_1 (.a(a[0]), .b(b[0]), .sum(out[0]), .carry(halfadder_1_carry));
  FullAdder fulladder_1 (.c(halfadder_1_carry), .b(a[1]), .a(b[1]), .sum(out[1]), .carry(fulladder_1_carry));
  FullAdder fulladder_2 (.c(fulladder_1_carry), .b(a[2]), .a(b[2]), .sum(out[2]), .carry(fulladder_2_carry));
  FullAdder fulladder_3 (.c(fulladder_2_carry), .b(a[3]), .a(b[3]), .sum(out[3]), .carry(fulladder_3_carry));
  FullAdder fulladder_4 (.c(fulladder_3_carry), .b(a[4]), .a(b[4]), .sum(out[4]), .carry(fulladder_4_carry));
  FullAdder fulladder_5 (.c(fulladder_4_carry), .b(a[5]), .a(b[5]), .sum(out[5]), .carry(fulladder_5_carry));
  FullAdder fulladder_6 (.c(fulladder_5_carry), .b(a[6]), .a(b[6]), .sum(out[6]), .carry(fulladder_6_carry));
  FullAdder fulladder_7 (.c(fulladder_6_carry), .b(a[7]), .a(b[7]), .sum(out[7]), .carry(fulladder_7_carry));
  FullAdder fulladder_8 (.c(fulladder_7_carry), .b(a[8]), .a(b[8]), .sum(out[8]), .carry(fulladder_8_carry));
  FullAdder fulladder_9 (.c(fulladder_8_carry), .b(a[9]), .a(b[9]), .sum(out[9]), .carry(fulladder_9_carry));
  FullAdder fulladder_10 (.c(fulladder_9_carry), .b(a[10]), .a(b[10]), .sum(out[10]), .carry(fulladder_10_carry));
  FullAdder fulladder_11 (.c(fulladder_10_carry), .b(a[11]), .a(b[11]), .sum(out[11]), .carry(fulladder_11_carry));
  FullAdder fulladder_12 (.c(fulladder_11_carry), .b(a[12]), .a(b[12]), .sum(out[12]), .carry(fulladder_12_carry));
  FullAdder fulladder_13 (.c(fulladder_12_carry), .b(a[13]), .a(b[13]), .sum(out[13]), .carry(fulladder_13_carry));
  FullAdder fulladder_14 (.c(fulladder_13_carry), .b(a[14]), .a(b[14]), .sum(out[14]), .carry(fulladder_14_carry));
  FullAdder fulladder_15 (.c(fulladder_14_carry), .b(a[15]), .a(b[15]), .sum(out[15]));  // open: carry
endmodule

module Inc16 (
  input  [15:0] in,
  output [15:0] out
);

  Add16 add16_1 (.a(in), .b(16'h1), .out(out));
endmodule

module ALU (
  input  zx,
  input  zy,
  input  nx,
  input  ny,
  input  f,
  input  no,
  input  [15:0] x,
  input  [15:0] y,
  output [15:0] out,
  output zr,
  output ng
);

  wire or8way_1_out, or8way_2_out, or_1_out;
  wire [15:0] Add16_out, and_1_out, multiplexer_1_out, multiplexer_2_out, multiplexer_3_out,
       multiplexer_4_out, multiplexer_5_out, not_2_out, not_3_out, not_4_out;

  Multiplexer #(.width(16), .enable("false")) multiplexer_1 (
    .in0(x), .in1({16{1'b0}}), .out(multiplexer_1_out), .sel(zx));
  Multiplexer #(.width(16), .enable("false")) multiplexer_2 (
    .in0(y), .in1({16{1'b0}}), .out(multiplexer_2_out), .sel(zy));
  not not_1 (zr, or_1_out);
  assign not_2_out = ~multiplexer_1_out;  // NOT_Gate not_2, 16 bits wide
  assign not_3_out = ~multiplexer_2_out;  // NOT_Gate not_3, 16 bits wide
  or or_1 (or_1_out, or8way_1_out, or8way_2_out);
  Multiplexer #(.width(16), .enable("false")) multiplexer_3 (
    .in0(multiplexer_1_out), .in1(not_2_out), .out(multiplexer_3_out), .sel(nx));
  Multiplexer #(.width(16), .enable("false")) multiplexer_4 (
    .in0(multiplexer_2_out), .in1(not_3_out), .out(multiplexer_4_out), .sel(ny));
  Or8Way or8way_1 (.in(out[7:0]), .out(or8way_1_out));
  Or8Way or8way_2 (.in({ng, out[14:8]}), .out(or8way_2_out));
  assign and_1_out = multiplexer_4_out & multiplexer_3_out;  // AND_Gate and_1, 16 bits wide
  Add16 Add16 (.a(multiplexer_3_out), .b(multiplexer_4_out), .out(Add16_out));
  Multiplexer #(.width(16), .enable("false")) multiplexer_5 (
    .in0(and_1_out), .in1(Add16_out), .out(multiplexer_5_out), .sel(f));
  Multiplexer #(.width(16), .enable("false")) multiplexer_6 (
    .in0(multiplexer_5_out), .in1(not_4_out), .out({ng, out[14:0]}), .sel(no));
  assign not_4_out = ~multiplexer_5_out;  // NOT_Gate not_4, 16 bits wide

  assign out[15] = ng;

  // Notes on the sheet:
  //   xzx
  //   yzy
  //   notor15
  //   notxzx
  //   notyzy
  //   or015
  //   xnx
  //   yny
  //   or07
  //   or715
  //   xandy
  //   xaddy
  //   fxy
  //   notfxy
  //   noxy
endmodule
