// Logisim project chapter3.circ as structural Verilog
module Bit (
  input  load,
  input  in,
  output out
);

  wire clock_1_out, multiplexer_1_out;

  Clock clock_1 (.out(clock_1_out));
  Multiplexer #(.enable("false")) multiplexer_1 (.in0(out), .in1(in), .out(multiplexer_1_out), .sel(load));
  D_Flip_Flop #(.trigger("falling")) d_ff_1 (
    .clk(clock_1_out), .D(multiplexer_1_out), .Q(out));  // open: Qn, preset, en, reset
endmodule

module PC (
  input  reset,
  input  load,
  input  inc,
  input  [15:0] in,
  output [15:0] out
);

  wire clock_1_out, or_1_out;
  wire [15:0] inc16_1_out, multiplexer_1_out, multiplexer_2_out, multiplexer_3_out;

  Inc16 inc16_1 (.in(out), .out(inc16_1_out));
  Multiplexer #(.width(16), .enable("false")) multiplexer_1 (
    .in0(in), .in1(inc16_1_out), .out(multiplexer_1_out), .sel(inc));
  Multiplexer #(.width(16), .enable("false")) multiplexer_2 (
    .in0(multiplexer_1_out), .in1(in), .out(multiplexer_2_out), .sel(load));
  or or_1 (or_1_out, reset, load, inc);
  Multiplexer #(.width(16), .enable("false")) multiplexer_3 (
    .in0(multiplexer_2_out), .in1({16{1'b0}}), .out(multiplexer_3_out), .sel(reset));
  Clock clock_1 (.out(clock_1_out));
  Register register_1 (.in(multiplexer_3_out), .load(or_1_out), .clock(clock_1_out), .out(out));
endmodule

module Register (
  input  [15:0] in,
  input  load,
  input  clock,
  output [15:0] out
);

  Register_part #(.width(1)) register_1 (.D(in[0]), .en(load), .Q(out[0]), .clk(clock));  // open: clr
  Register_part #(.width(1)) register_2 (.D(in[1]), .en(load), .Q(out[1]), .clk(clock));  // open: clr
  Register_part #(.width(1)) register_3 (.D(in[2]), .en(load), .Q(out[2]), .clk(clock));  // open: clr
  Register_part #(.width(1)) register_4 (.D(in[3]), .en(load), .Q(out[3]), .clk(clock));  // open: clr
  Register_part #(.width(1)) register_5 (.D(in[12]), .en(load), .Q(out[12]), .clk(clock));  // open: clr
  Register_part #(.width(1)) register_6 (.D(in[13]), .en(load), .Q(out[13]), .clk(clock));  // open: clr
  Register_part #(.width(1)) register_7 (.D(in[14]), .en(load), .Q(out[14]), .clk(clock));  // open: clr
  Register_part #(.width(1)) register_8 (.D(in[15]), .en(load), .Q(out[15]), .clk(clock));  // open: clr
  Register_part #(.width(1)) register_9 (.D(in[4]), .en(load), .Q(out[4]), .clk(clock));  // open: clr
  Register_part #(.width(1)) register_10 (.D(in[5]), .en(load), .Q(out[5]), .clk(clock));  // open: clr
  Register_part #(.width(1)) register_11 (.D(in[6]), .en(load), .Q(out[6]), .clk(clock));  // open: clr
  Register_part #(.width(1)) register_12 (.D(in[7]), .en(load), .Q(out[7]), .clk(clock));  // open: clr
  Register_part #(.width(1)) register_13 (.D(in[8]), .en(load), .Q(out[8]), .clk(clock));  // open: clr
  Register_part #(.width(1)) register_14 (.D(in[9]), .en(load), .Q(out[9]), .clk(clock));  // open: clr
  Register_part #(.width(1)) register_15 (.D(in[10]), .en(load), .Q(out[10]), .clk(clock));  // open: clr
  Register_part #(.width(1)) register_16 (.D(in[11]), .en(load), .Q(out[11]), .clk(clock));  // open: clr
endmodule

module Ram8 (
  input  load,
  input  [15:0] in,
  input  [2:0] address,
  input  clock,
  output [15:0] out
);

  wire demultiplexer_1_out0, demultiplexer_1_out1, demultiplexer_1_out2, demultiplexer_1_out3,
       demultiplexer_1_out4, demultiplexer_1_out5, demultiplexer_1_out6, demultiplexer_1_out7;
  wire [15:0] register_1_q, register_2_q, register_3_q, register_4_q, register_5_q, register_6_q,
       register_7_q, register_8_q;

  Demultiplexer #(.select(3), .enable("false")) demultiplexer_1 (
    .out0(demultiplexer_1_out0), .out1(demultiplexer_1_out1), .out2(demultiplexer_1_out2),
    .out3(demultiplexer_1_out3), .out4(demultiplexer_1_out4), .out5(demultiplexer_1_out5),
    .out6(demultiplexer_1_out6), .out7(demultiplexer_1_out7), .in(load), .sel(address));
  Register_part #(.width(16)) register_1 (
    .D(in), .en(demultiplexer_1_out0), .Q(register_1_q), .clk(clock));  // open: clr
  Register_part #(.width(16)) register_2 (
    .D(in), .en(demultiplexer_1_out1), .Q(register_2_q), .clk(clock));  // open: clr
  Register_part #(.width(16)) register_3 (
    .D(in), .en(demultiplexer_1_out2), .Q(register_3_q), .clk(clock));  // open: clr
  Register_part #(.width(16)) register_4 (
    .D(in), .en(demultiplexer_1_out3), .Q(register_4_q), .clk(clock));  // open: clr
  Register_part #(.width(16)) register_5 (
    .D(in), .en(demultiplexer_1_out4), .Q(register_5_q), .clk(clock));  // open: clr
  Register_part #(.width(16)) register_6 (
    .D(in), .en(demultiplexer_1_out5), .Q(register_6_q), .clk(clock));  // open: clr
  Register_part #(.width(16)) register_7 (
    .D(in), .en(demultiplexer_1_out6), .Q(register_7_q), .clk(clock));  // open: clr
  Register_part #(.width(16)) register_8 (
    .D(in), .en(demultiplexer_1_out7), .Q(register_8_q), .clk(clock));  // open: clr
  Multiplexer #(.select(3), .width(16), .enable("false")) multiplexer_1 (
    .in0(register_1_q), .in1(register_2_q), .in2(register_3_q), .in3(register_4_q), .in4(register_5_q),
    .in5(register_6_q), .in6(register_7_q), .in7(register_8_q), .out(out), .sel(address));
endmodule

module RAM64 (
  input  load,
  input  [15:0] in,
  input  [5:0] address,
  input  clock,
  output [15:0] in_2
);

  wire demultiplexer_1_out0, demultiplexer_1_out1, demultiplexer_1_out2, demultiplexer_1_out3,
       demultiplexer_1_out4, demultiplexer_1_out5, demultiplexer_1_out6, demultiplexer_1_out7;
  wire [15:0] ram8_1_out, ram8_2_out, ram8_3_out, ram8_4_out, ram8_5_out, ram8_6_out, ram8_7_out, ram8_8_out;

  Demultiplexer #(.select(3), .enable("false")) demultiplexer_1 (
    .out0(demultiplexer_1_out0), .out1(demultiplexer_1_out1), .out2(demultiplexer_1_out2),
    .out3(demultiplexer_1_out3), .out4(demultiplexer_1_out4), .out5(demultiplexer_1_out5),
    .out6(demultiplexer_1_out6), .out7(demultiplexer_1_out7), .in(load), .sel(address[2:0]));
  Ram8 ram8_1 (.load(demultiplexer_1_out0), .in(in), .address(address[5:3]), .clock(clock), .out(ram8_1_out));
  Ram8 ram8_2 (.load(demultiplexer_1_out1), .in(in), .address(address[5:3]), .clock(clock), .out(ram8_2_out));
  Ram8 ram8_3 (.load(demultiplexer_1_out2), .in(in), .address(address[5:3]), .clock(clock), .out(ram8_3_out));
  Ram8 ram8_4 (.load(demultiplexer_1_out3), .in(in), .address(address[5:3]), .clock(clock), .out(ram8_4_out));
  Ram8 ram8_5 (.load(demultiplexer_1_out4), .in(in), .address(address[5:3]), .clock(clock), .out(ram8_5_out));
  Ram8 ram8_6 (.load(demultiplexer_1_out5), .in(in), .address(address[5:3]), .clock(clock), .out(ram8_6_out));
  Ram8 ram8_7 (.load(demultiplexer_1_out6), .in(in), .address(address[5:3]), .clock(clock), .out(ram8_7_out));
  Ram8 ram8_8 (.load(demultiplexer_1_out7), .in(in), .address(address[5:3]), .clock(clock), .out(ram8_8_out));
  Multiplexer #(.select(3), .width(16), .enable("false")) multiplexer_1 (
    .in0(ram8_1_out), .in1(ram8_2_out), .in2(ram8_3_out), .in3(ram8_4_out), .in4(ram8_5_out),
    .in5(ram8_6_out), .in6(ram8_7_out), .in7(ram8_8_out), .out(in_2), .sel(address[2:0]));
endmodule

module Ram512 (
  input  in_1,
  input  [15:0] in,
  input  [8:0] in_3,
  input  clock,
  output [15:0] in_2
);

  wire demultiplexer_1_out0, demultiplexer_1_out1, demultiplexer_1_out2, demultiplexer_1_out3,
       demultiplexer_1_out4, demultiplexer_1_out5, demultiplexer_1_out6, demultiplexer_1_out7;
  wire [15:0] ram64_1_in_2, ram64_2_in_2, ram64_3_in_2, ram64_4_in_2, ram64_5_in_2, ram64_6_in_2,
       ram64_7_in_2, ram64_8_in_2;

  Demultiplexer #(.select(3), .enable("false")) demultiplexer_1 (
    .out0(demultiplexer_1_out0), .out1(demultiplexer_1_out1), .out2(demultiplexer_1_out2),
    .out3(demultiplexer_1_out3), .out4(demultiplexer_1_out4), .out5(demultiplexer_1_out5),
    .out6(demultiplexer_1_out6), .out7(demultiplexer_1_out7), .in(in_1), .sel(in_3[2:0]));
  RAM64 ram64_1 (.load(demultiplexer_1_out0), .in(in), .address(in_3[8:3]), .clock(clock), .in_2(ram64_1_in_2));
  RAM64 ram64_2 (.load(demultiplexer_1_out1), .in(in), .address(in_3[8:3]), .clock(clock), .in_2(ram64_2_in_2));
  RAM64 ram64_3 (.load(demultiplexer_1_out2), .in(in), .address(in_3[8:3]), .clock(clock), .in_2(ram64_3_in_2));
  RAM64 ram64_4 (.load(demultiplexer_1_out3), .in(in), .address(in_3[8:3]), .clock(clock), .in_2(ram64_4_in_2));
  RAM64 ram64_5 (.load(demultiplexer_1_out4), .in(in), .address(in_3[8:3]), .clock(clock), .in_2(ram64_5_in_2));
  RAM64 ram64_6 (.load(demultiplexer_1_out5), .in(in), .address(in_3[8:3]), .clock(clock), .in_2(ram64_6_in_2));
  RAM64 ram64_7 (.load(demultiplexer_1_out6), .in(in), .address(in_3[8:3]), .clock(clock), .in_2(ram64_7_in_2));
  RAM64 ram64_8 (.load(demultiplexer_1_out7), .in(in), .address(in_3[8:3]), .clock(clock), .in_2(ram64_8_in_2));
  Multiplexer #(.select(3), .width(16), .enable("false")) multiplexer_1 (
    .in0(ram64_1_in_2), .in1(ram64_2_in_2), .in2(ram64_3_in_2), .in3(ram64_4_in_2), .in4(ram64_5_in_2),
    .in5(ram64_6_in_2), .in6(ram64_7_in_2), .in7(ram64_8_in_2), .out(in_2), .sel(in_3[2:0]));
endmodule

module RAM4K (
  input  in_1,
  input  [15:0] in,
  input  [11:0] in_3,
  input  clock,
  output [15:0] in_2
);

  wire demultiplexer_1_out0, demultiplexer_1_out1, demultiplexer_1_out2, demultiplexer_1_out3,
       demultiplexer_1_out4, demultiplexer_1_out5, demultiplexer_1_out6, demultiplexer_1_out7;
  wire [15:0] ram512_1_in_2, ram512_2_in_2, ram512_3_in_2, ram512_4_in_2, ram512_5_in_2, ram512_6_in_2,
       ram512_7_in_2, ram512_8_in_2;

  Demultiplexer #(.select(3), .enable("false")) demultiplexer_1 (
    .out0(demultiplexer_1_out0), .out1(demultiplexer_1_out1), .out2(demultiplexer_1_out2),
    .out3(demultiplexer_1_out3), .out4(demultiplexer_1_out4), .out5(demultiplexer_1_out5),
    .out6(demultiplexer_1_out6), .out7(demultiplexer_1_out7), .in(in_1), .sel(in_3[2:0]));
  Ram512 ram512_1 (.in_1(demultiplexer_1_out0), .in(in), .in_3(in_3[11:3]), .clock(clock), .in_2(ram512_1_in_2));
  Ram512 ram512_2 (.in_1(demultiplexer_1_out1), .in(in), .in_3(in_3[11:3]), .clock(clock), .in_2(ram512_2_in_2));
  Ram512 ram512_3 (.in_1(demultiplexer_1_out2), .in(in), .in_3(in_3[11:3]), .clock(clock), .in_2(ram512_3_in_2));
  Ram512 ram512_4 (.in_1(demultiplexer_1_out3), .in(in), .in_3(in_3[11:3]), .clock(clock), .in_2(ram512_4_in_2));
  Ram512 ram512_5 (.in_1(demultiplexer_1_out4), .in(in), .in_3(in_3[11:3]), .clock(clock), .in_2(ram512_5_in_2));
  Ram512 ram512_6 (.in_1(demultiplexer_1_out5), .in(in), .in_3(in_3[11:3]), .clock(clock), .in_2(ram512_6_in_2));
  Ram512 ram512_7 (.in_1(demultiplexer_1_out6), .in(in), .in_3(in_3[11:3]), .clock(clock), .in_2(ram512_7_in_2));
  Ram512 ram512_8 (.in_1(demultiplexer_1_out7), .in(in), .in_3(in_3[11:3]), .clock(clock), .in_2(ram512_8_in_2));
  Multiplexer #(.select(3), .width(16), .enable("false")) multiplexer_1 (
    .in0(ram512_1_in_2), .in1(ram512_2_in_2), .in2(ram512_3_in_2), .in3(ram512_4_in_2), .in4(ram512_5_in_2),
    .in5(ram512_6_in_2), .in6(ram512_7_in_2), .in7(ram512_8_in_2), .out(in_2), .sel(in_3[2:0]));
endmodule

module RAM16K (
  input  in_1,
  input  [15:0] in,
  input  [13:0] in_3,
  input  clock,
  output [15:0] in_2
);

  wire demultiplexer_1_out0, demultiplexer_1_out1, demultiplexer_1_out2, demultiplexer_1_out3;
  wire [15:0] ram4k_1_in_2, ram4k_2_in_2, ram4k_3_in_2, ram4k_4_in_2;

  Demultiplexer #(.select(2), .enable("false")) demultiplexer_1 (
    .out0(demultiplexer_1_out0), .out1(demultiplexer_1_out1), .out2(demultiplexer_1_out2),
    .out3(demultiplexer_1_out3), .in(in_1), .sel(in_3[1:0]));
  RAM4K ram4k_1 (.in_1(demultiplexer_1_out0), .in(in), .in_3(in_3[13:2]), .clock(clock), .in_2(ram4k_1_in_2));
  RAM4K ram4k_2 (.in_1(demultiplexer_1_out1), .in(in), .in_3(in_3[13:2]), .clock(clock), .in_2(ram4k_2_in_2));
  RAM4K ram4k_3 (.in_1(demultiplexer_1_out2), .in(in), .in_3(in_3[13:2]), .clock(clock), .in_2(ram4k_3_in_2));
  RAM4K ram4k_4 (.in_1(demultiplexer_1_out3), .in(in), .in_3(in_3[13:2]), .clock(clock), .in_2(ram4k_4_in_2));
  Multiplexer #(.select(2), .width(16), .enable("false")) multiplexer_1 (
    .in0(ram4k_1_in_2), .in1(ram4k_2_in_2), .in2(ram4k_3_in_2), .in3(ram4k_4_in_2), .out(in_2),
    .sel(in_3[1:0]));
endmodule
